// Logisim project cpu.circ as structural Verilog: 3 circuits, main circuit d-latch
module d_latch (
  input  in_1,
  input  in_2,
  output Q,
  output Q_prime
);

  wire and_1_out, and_2_out, nor_1_out, nor_2_out, not_1_out;

  not not_1 (not_1_out, in_2);
  and and_1 (and_1_out, not_1_out, in_1);
  and and_2 (and_2_out, in_1, in_2);
  nor nor_1 (nor_1_out, and_1_out, nor_2_out);
  nor nor_2 (nor_2_out, nor_1_out, and_2_out);
endmodule

module d_flip_flop (
  input  d,
  output q,
  output q_prime
);

  wire clock_1_out, d_latch_1_q_prime, not_1_out, not_2_out;

  Clock clock_1 (.out(clock_1_out));
  d_latch d_latch_1 (.Q_prime(d_latch_1_q_prime), .in_2(d), .in_1(not_1_out));  // open: Q
  not not_1 (not_1_out, clock_1_out);
  not not_2 (not_2_out, not_1_out);
  d_latch d_latch_2 (.Q(q), .Q_prime(q_prime), .in_2(d_latch_1_q_prime), .in_1(not_2_out));
endmodule

module full_adder_1_bit (
  input  bit_1st,
  input  bit_2nd,
  input  carry_in,
  output carry_out,
  output result
);

  wire and_1_out, and_2_out, and_3_out;

  and and_1 (and_1_out, bit_1st, bit_2nd);
  and and_2 (and_2_out, bit_2nd, carry_in);
  and and_3 (and_3_out, bit_1st, carry_in);
  ExactlyOne xor_1 (.out(result), .in0(bit_1st), .in1(bit_2nd), .in2(carry_in));
  or or_1 (carry_out, and_1_out, and_2_out, and_3_out);
endmodule
